# Fritzing sketch 3 - Connect the DHT11 (saved by Fritzing 0.9.2b)
breadboards: 1

parts:
  Part1 = Arduino Uno (Rev3) - ICSP
  CC3K1 = Adafruit CC3000 WiFi Breakout
  DHT1 = DHT11 Humitidy and Temperature Sensor
  R1 = Resistor [tolerance=±5% resistance=10k package=THT]

nets:
  N1: Part1.D10_PWM/SS, CC3K1.CS
  N2: Part1.D11_PWM/MOSI, CC3K1.MOSI
  N3: Part1.D12/MISO, CC3K1.MISO
  N4: Part1.D13/SCK, CC3K1.CLK
  N5: Part1.D3_PWM, CC3K1.IRQ
  5V: Part1.D6_PWM, Part1.5V, CC3K1.VBEN, DHT1.VDD, R1.Pin_0
  N6: Part1.D7, DHT1.DATA, R1.Pin_1
  GND: Part1.GND, CC3K1.GND, DHT1.GND
  N7: CC3K1.TXD, CC3K1.RXD

custom parts:
  Adafruit CC3000 WiFi Breakout: CC3000 WiFi Breakout
  DHT11 Humitidy and Temperature Sensor: DHT11 Humidity and Temperature Sensor
